# Fritzing sketch casa-domotica1 (saved by Fritzing 0.9.3b)

parts:
  Componente1 = Arduino Uno (Rev3)
  VCC1 = Battery
  J1 = Basic Servo
  J2 = Basic Servo
  J3 = Basic Servo
  J4 = Basic Servo
  KY-1 = Keyes Relay [package=THT]
  KY-2 = Keyes Relay [package=THT]
  KY-3 = Keyes Relay [package=THT]
  KY-4 = Keyes Relay [package=THT]
  LED1 = LEDs [package=led10mm]
  LED2 = LEDs [package=led10mm]
  LED3 = LEDs [package=led10mm]
  LED4 = LEDs [package=led10mm]
  VCC2 = 4 x AAA Battery Mount  # not connected

nets:
  N1: Componente1.D8, J1.pulse
  N2: Componente1.D1/TX, KY-4.signal
  N3: Componente1.D2, KY-3.signal
  N4: Componente1.D3_PWM, KY-2.signal
  N5: Componente1.D4, KY-1.signal
  N6: Componente1.D5_PWM, J4.pulse
  N7: Componente1.D6_PWM, J3.pulse
  N8: Componente1.D7, J2.pulse
  N9: VCC1.-, KY-1.ground, KY-1.C, KY-2.C, KY-3.C, KY-4.ground, KY-4.C
  N10: VCC1.+, KY-1.power, KY-3.NO, KY-4.power, LED1.A, LED2.A, LED3.A, LED3.C, LED4.A
  N11: KY-1.NO, LED1.C
  N12: KY-2.NO, LED2.C
  N13: KY-4.NO, LED4.C

custom parts:
  Keyes Relay: The Keyes 5V relay module is suitable for SCM development, home appliance control. It uses a 5V~12V TIL control signal which can control DC / AC signal.
  LEDs: LEDs Standard schematic elements and footprints for 5mm, 3mm, 1206, and 0603 sized LEDs. 5mm - Spark Fun Electronics SKU : COM-00529 (and others)
